# Fritzing sketch ManageLED (saved by Fritzing 0.9.2b)
breadboards: 1

parts:
  Part1 = DragonBoard Low Speed Expansion Connector [form="♂ (male)" package=THT]
  LED1 = LED - 5mm [color="Red (633nm)" package="5 mm [THT]"]
  R1 = Resistor [tolerance=±5% resistance=50m package="0603 [SMD]"]
  PART1 = SparkFun Voltage-Level Translator Breakout - TXB0104 [part_number=BOB-11771]

nets:
  N1: Part1.pin24, PART1.VCCA
  N2: Part1.pin37, R1.Pin_0, PART1.VCCB
  N3: Part1.pin40, PART1.GND#13
  N4: LED1.cathode, PART1.GND#12
  N5: LED1.anode, R1.Pin_1

custom parts:
  DragonBoard Low Speed Expansion Connector: DragonBoard low speed expansion connector
  SparkFun Voltage-Level Translator Breakout - TXB0104: This is a breakout board for the Texas Instruments TXB0104 module. The TXB0104 is a 4-bit bidirectional voltage-level translator with automatic direction sensing. This 4-bit noninverting translator uses two separate configurable power-supply rails. The A port is designed to track VCCA. VCCA accepts any supply voltage from 1.2V to 3.6V. The B port is designed to track VCCB. VCCB accepts any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
