# Fritzing sketch ManageLED (saved by Fritzing 0.9.2b)
breadboards: 1

parts:
  Part1 = DragonBoard Low Speed Expansion Connector [form="♂ (male)" package=THT]
  LED1 = LED - 5mm [color="Red (633nm)" package="5 mm [THT]"]
  R1 = Resistor [tolerance=±5% resistance=50m package="0603 [SMD]"]

nets:
  N1: Part1.pin2, LED1.cathode
  N2: Part1.pin24, R1.Pin_0
  N3: LED1.anode, R1.Pin_1

custom parts:
  DragonBoard Low Speed Expansion Connector: DragonBoard low speed expansion connector
